# Fritzing sketch electronic-gas-mask-filter (saved by Fritzing 1.0.5)
# 18650 Li-ion Battery: CC-BY Dr Kristofer Chan, King's College London/Remote-research.org
circuit board: 8.46667cm x 5.64444cm
breadboards: 1

parts:
  BAT1 = 18650 Li-ion Battery [package=battery-18650]
  M1 = MT3608 Module
  Компонент1 = Arduino Pro Mini (3.3V)
  C1 = Ceramic Capacitor [capacitance=10µF voltage=6.3V package="100 mil [THT, multilayer]"]
  C2 = Electrolytic Capacitor [capacitance=47µF voltage=6.3V package="100 mil [THT, electrolytic]"]
  SW1 = DIP Switch 8 Position [package=dipswitch-08]
  CounterB = Momentary Switch [package=ksa_sealed_tac_switch]
  C3 = Ceramic Capacitor [capacitance=100nF voltage=6.3V mn=(104) package="0603 [SMD, multilayer]"]
  R1 = Resistor [tolerance=±5% power=0.25W resistance=220 package=THT]
  ConfigB = Momentary Switch [package=ksa_sealed_tac_switch]
  C4 = Ceramic Capacitor [capacitance=100nF voltage=6.3V mn=(104) package="0603 [SMD, multilayer]"]
  R2 = Resistor [tolerance=±5% power=0.25W resistance=220 package=THT]
  LED1 = smd LED [color="Red (633nm)" package="0805 [SMD]"]
  LED2 = Super Flux LED blue [color=Blue current=0.030A]
  R3 = Resistor [tolerance=±5% resistance=100 package="0805 [SMD]"]
  R4 = Resistor [tolerance=±5% resistance=100 package="0805 [SMD]"]
  J1 = Piezo Speaker

nets (from the breadboard view):
  N1: BAT1.-, M1.pin1
  N2: BAT1.+, M1.pin2
  N3: M1.pin3, Компонент1.RAW, C1.0, C2.-
  N4: M1.pin4, Компонент1.GND, C1.1, C2.+, SW1.13, SW1.14, SW1.15, SW1.16, CounterB.1, CounterB.2, R1.Pin_0, ConfigB.1, ConfigB.2, R2.Pin_0, LED1.cathode, LED2.cathode, J1.pin1
  N5: Компонент1.SCK, J1.pin2
  N6: Компонент1.MISO, R3.Pin_1
  N7: Компонент1.MOSI, R4.Pin_1
  N8: Компонент1.D7, SW1.1
  N9: Компонент1.D6, SW1.2
  N10: Компонент1.D5, SW1.3
  N11: Компонент1.D4, SW1.4
  N12: Компонент1.D3, ConfigB.3, ConfigB.4, C4.1
  N13: Компонент1.D2, CounterB.3, CounterB.4, C3.1
  N14: C4.0, R2.Pin_1
  N15: LED1.anode, R4.Pin_0
  N16: LED2.anode, R3.Pin_0

custom parts:
  18650 Li-ion Battery: 18650 li-ion Battery Standard 18650 battery with interactive connectors Creative Common Attribution 4.0 International (CC-BY 4.0) license. Any use of this part requires attribution of Dr Kristofer Chan, Department of Geography, King's College London. Contact kristofer.chan [at] kcl.ac.uk OR kris [at] remote-research.org for further information.
  MT3608 Module: MT3608 Boost Converter Module Links: Aerosemi MT3608 2A Step Up Converter datasheet

// code stored in the sketch: electronic-gas-mask-filter.ino
#include "src/Button.h"
#include "src/MinimalEEPROM.h"
#include "src/ConfigurationModule.h"
#include "src/MainCounterModule.h"
#include "src/IndicationModule.h"

//******* Работа с памятью EEPROM *******
MinimalEEPROM eeprom;

//******* МОДУЛЬ ИНДИКАЦИИ *******
// Объявляем модуль индикации со светодиодами (green, red) и пищалкой (buzzer)
IndicationModule indicationModule(11, 12, 13);

//******* МОДУЛЬ КОНФИГУРАЦИИ *******
// Кнопка - конфигурация, сброс
Button configurationButton(3, 1500, 50);
// Массив пинов DIP-переключателя
uint8_t DIPPins[] = { 7, 6, 5, 4 };
// Обьявляем модуль конфигурации
ConfigurationModule configurationModule(configurationButton, eeprom, DIPPins, indicationModule);

//******* ГЛАВНЫЙ МОДУЛЬ *******
// Кнопка - старт счетчика
Button counterButton(2);
// Объявляем модуль счетчика
MainCounterModule mainCounterModule(counterButton, eeprom, indicationModule);

void setup() {
  // Инициализация модуля индикации
  indicationModule.begin();
  // Инициализация модуля конфигурации
  configurationModule.begin();
  // Инициализация модуля счетчика
  mainCounterModule.begin();
}

void loop() {
  // Обновление состояния индикаторов
  indicationModule.update();

  // Обрабатываем конфигурацию
  configurationModule.update();
  if (configurationModule.isActive()) {
    return;  // корректно выходим в окно в режиме конфигурации
  }

  // Обрабатываем счетчик
  mainCounterModule.update();
}
